// Logisim project kocka.circ as structural Verilog: 1 circuit, main circuit Decoder - MultiDice
module Decoder___MultiDice (
  output D4,
  output D6,
  output D8,
  output D10,
  output out_5,
  output out_6,
  output out_7,
  output out_8,
  output out_9,
  output out_10,
  output out_11,
  output out_12,
  output out_13
);

  wire and_1_out, and_2_out, and_3_out, and_4_out, and_5_out, BTN_out, CLK_out, decoder_1_out0,
       decoder_1_out1, decoder_1_out2, decoder_1_out3, decoder_1_out4, decoder_1_out5, decoder_1_out6,
       decoder_1_out7, decoder_1_out8, decoder_1_out10, or_1_out, SET_out;
  wire [1:0] counter_1_q;
  wire [3:0] counter_2_q;

  Button BTN (.out(BTN_out));
  and and_1 (and_1_out, BTN_out, CLK_out);
  Clock CLK (.out(CLK_out));
  Button SET (.out(SET_out));
  Counter #(.width(2), .max('h3)) counter_1 (.Q(counter_1_q), .clk(SET_out));  // open: load, D, count, carry, clr
  Counter #(.width(4), .max('hf)) counter_2 (
    .Q(counter_2_q), .clk(and_1_out), .clr(or_1_out));  // open: load, D, count, carry
  or or_1 (or_1_out, SET_out, and_2_out, and_3_out, and_4_out, and_5_out);
  Demultiplexer #(.select(2), .enable("false")) demultiplexer_1 (
    .out0(D4), .out1(D6), .out2(D8), .out3(D10), .in(1'b1), .sel(counter_1_q));
  Decoder #(.select(4), .enable("false")) decoder_1 (
    .out0(decoder_1_out0), .out1(decoder_1_out1), .out2(decoder_1_out2), .out3(decoder_1_out3),
    .out4(decoder_1_out4), .out5(decoder_1_out5), .out6(decoder_1_out6), .out7(decoder_1_out7),
    .out8(decoder_1_out8), .out10(decoder_1_out10), .sel(counter_2_q));  // open: out9, out11, out12, out13, out14, out15
  and and_2 (and_2_out, D4, decoder_1_out4);
  and and_3 (and_3_out, D6, decoder_1_out6);
  and and_4 (and_4_out, D8, decoder_1_out8);
  and and_5 (and_5_out, D10, decoder_1_out10);
  or or_2 (out_5, decoder_1_out1, decoder_1_out3, decoder_1_out4, decoder_1_out5, decoder_1_out6, decoder_1_out7, decoder_1_out8);
  or or_3 (out_6, decoder_1_out5, decoder_1_out6, decoder_1_out7, decoder_1_out8);
  or or_4 (out_7, decoder_1_out2, decoder_1_out3, decoder_1_out4, decoder_1_out5, decoder_1_out6, decoder_1_out7, decoder_1_out8);
  or or_5 (out_8, decoder_1_out7, decoder_1_out8);
  or or_6 (out_10, decoder_1_out0, decoder_1_out2, decoder_1_out4, decoder_1_out6, decoder_1_out8);
  or or_7 (out_12, decoder_1_out5, decoder_1_out6, decoder_1_out7, decoder_1_out8);

  assign out_9 = out_8;
  assign out_11 = out_7;
  assign out_13 = out_5;
endmodule
